# Fritzing sketch attiny85-ledOn (saved by Fritzing 0.9.3b)
circuit board: 8.46667cm x 5.64444cm
breadboards: 1

parts:
  U1 = attiny85 [package=dip]
  VCC1 = Battery
  R1 = Resistor [tolerance=±5% resistance=220 package=THT]
  R2 = Resistor [tolerance=±5% resistance=220 package=THT]
  LED1 = LED - 5mm [color="Red (633nm)" package="5 mm [THT]"]

nets:
  N1: U1.Pin_1, R1.Pin_0
  N2: U1.Pin_4, VCC1.-, LED1.cathode
  N3: U1.Pin_5, R2.Pin_0
  N4: U1.Pin_8, VCC1.+, R1.Pin_1
  N5: R2.Pin_1, LED1.anode
